# Fritzing sketch Skema LED (saved by Fritzing 0.8.7b)
breadboards: 2

parts:
  Raspberry_Pi_A1 = Raspberry Pi A
  S1 = Momentary Switch [package=ksa_sealed_tac_switch]
  LED1 = smd LED [color="Yellow (595nm)" package="0603 [SMD]"]
  LED1_2 = smd LED [color="Red (633nm)" package="0805 [SMD]"]
  LED2 = smd LED [color="Green (570nm)" package="0805 [SMD]"]
  LED3 = smd LED [color="Red (633nm)" package="0805 [SMD]"]
  LED4 = smd LED [color="Green (570nm)" package="0805 [SMD]"]
  LED5 = smd LED [color="Yellow (595nm)" package="0603 [SMD]"]
  LED6 = smd LED [color="Red (633nm)" package="0805 [SMD]"]
  LED7 = smd LED [color="Green (570nm)" package="0805 [SMD]"]
  LED8 = smd LED [color="Yellow (595nm)" package="0603 [SMD]"]
  LED9 = smd LED [color="Red (633nm)" package="0805 [SMD]"]
  LED10 = smd LED [color="Green (570nm)" package="0805 [SMD]"]
  LED11 = smd LED [color="Yellow (595nm)" package="0603 [SMD]"]

nets:
  N1: Raspberry_Pi_A1.GPIO_23, S1.4
  N2: Raspberry_Pi_A1.GPIO_18, Raspberry_Pi_A1.GND, S1.2, LED1.cathode, LED1_2.cathode, LED2.cathode, LED3.cathode, LED4.cathode, LED5.cathode, LED6.cathode, LED7.cathode, LED8.cathode, LED9.cathode, LED10.cathode, LED11.cathode
  N3: Raspberry_Pi_A1.GPIO_27, LED2.anode, LED4.anode, LED7.anode, LED10.anode
  N4: Raspberry_Pi_A1.GPIO_24, LED1_2.anode, LED3.anode, LED6.anode, LED9.anode
  N5: Raspberry_Pi_A1.GPIO_25, LED1.anode, LED5.anode, LED8.anode, LED11.anode
